// Logisim project SUMADOR_RESTADOR_COMBINADO.circ as structural Verilog: 1 circuit, main circuit main
module main (
  input  [3:0] A_3_0,
  input  [3:0] B_3_0,
  input  Sel,
  output [3:0] Result_3_0,
  output Cout
);

  wire multiplexer_1_p3, not_1_p2;

  // NOT_Gate #(.width(4)) not_1: pin names not known; wires that end beside it: B_3_0, not_1_p2
  // Multiplexer #(.width(4), .selwidth(1)) multiplexer_1: pin names not known; wires that end beside it: not_1_p2, B_3_0, multiplexer_1_p3, not_1_p2, Sel
  // Adder #(.width(4)) adder_1: pin names not known; wires that end beside it: multiplexer_1_p3, Sel
endmodule
